# Fritzing sketch Servo and Ultrasonic (saved by Fritzing 0.9.3b)
breadboards: 1

parts:
  Part1 = Arduino Uno (Rev3)
  J1 = Basic Servo
  Sensor_1 = HC-SR04 Ultrasonic Distance Sensor

nets:
  N1: Part1.D10_PWM/SS, Sensor_1.TRIG
  N2: Part1.D11_PWM/MOSI, Sensor_1.ECHO
  N3: Part1.D12/MISO, J1.pulse
  GND: Part1.GND, J1.gnd, Sensor_1.GND
  VCC: Part1.5V, J1.vcc, Sensor_1.VCC
